// Logisim project 1721710042_AbrarRaiyan.circ as structural Verilog
module Register_File (
  input  [15:0] Write_Data,
  input  [3:0] Read_Register_1,
  input  [3:0] Write_Register,
  input  [3:0] Read_Register_2,
  input  Clock,
  input  Clear,
  input  Write_Enable,
  output [15:0] Read_Data_1,
  output [15:0] Read_Data_2
);

  wire and_1_out, and_2_out, and_3_out, and_4_out, and_5_out, and_6_out, and_7_out, and_8_out, and_9_out,
       and_10_out, and_11_out, and_12_out, and_13_out, and_14_out, and_15_out, and_16_out, decoder_1_out0,
       decoder_1_out1, decoder_1_out2, decoder_1_out3, decoder_1_out4, decoder_1_out5, decoder_1_out6,
       decoder_1_out7, decoder_1_out8, decoder_1_out9, decoder_1_out10, decoder_1_out11, decoder_1_out12,
       decoder_1_out13, decoder_1_out14, decoder_1_out15;
  wire [15:0] r1_0_q, r2_1_q, r3_2_q, r4_3_q, r5_4_q, r6_5_q, r7_6_q, r8_7_q, t1_8_q, t2_9_q, t3_10_q,
       t4_11_q, t5_12_q, t6_13_q, t7_14_q, t8_15_q;

  Decoder #(.select(4), .enable("false")) decoder_1 (
    .out0(decoder_1_out0), .out1(decoder_1_out1), .out2(decoder_1_out2), .out3(decoder_1_out3),
    .out4(decoder_1_out4), .out5(decoder_1_out5), .out6(decoder_1_out6), .out7(decoder_1_out7),
    .out8(decoder_1_out8), .out9(decoder_1_out9), .out10(decoder_1_out10), .out11(decoder_1_out11),
    .out12(decoder_1_out12), .out13(decoder_1_out13), .out14(decoder_1_out14), .out15(decoder_1_out15),
    .sel(Write_Register));
  and and_1 (and_1_out, Write_Enable, decoder_1_out0);
  and and_2 (and_2_out, Write_Enable, decoder_1_out1);
  and and_3 (and_3_out, Write_Enable, decoder_1_out2);
  and and_4 (and_4_out, Write_Enable, decoder_1_out3);
  and and_5 (and_5_out, Write_Enable, decoder_1_out4);
  and and_6 (and_6_out, Write_Enable, decoder_1_out5);
  and and_7 (and_7_out, Write_Enable, decoder_1_out6);
  and and_8 (and_8_out, Write_Enable, decoder_1_out7);
  and and_9 (and_9_out, Write_Enable, decoder_1_out8);
  and and_10 (and_10_out, Write_Enable, decoder_1_out9);
  and and_11 (and_11_out, Write_Enable, decoder_1_out10);
  and and_12 (and_12_out, Write_Enable, decoder_1_out11);
  and and_13 (and_13_out, Write_Enable, decoder_1_out12);
  and and_14 (and_14_out, Write_Enable, decoder_1_out13);
  and and_15 (and_15_out, Write_Enable, decoder_1_out14);
  and and_16 (and_16_out, Write_Enable, decoder_1_out15);
  Register #(.width(16)) r1_0 (.D(Write_Data), .en(and_1_out), .Q(r1_0_q), .clk(Clock), .clr(Clear));
  Register #(.width(16)) r2_1 (.D(Write_Data), .en(and_2_out), .Q(r2_1_q), .clk(Clock), .clr(Clear));
  Register #(.width(16)) r3_2 (.D(Write_Data), .en(and_3_out), .Q(r3_2_q), .clk(Clock), .clr(Clear));
  Register #(.width(16)) r4_3 (.D(Write_Data), .en(and_4_out), .Q(r4_3_q), .clk(Clock), .clr(Clear));
  Register #(.width(16)) r5_4 (.D(Write_Data), .en(and_5_out), .Q(r5_4_q), .clk(Clock), .clr(Clear));
  Register #(.width(16)) r6_5 (.D(Write_Data), .en(and_6_out), .Q(r6_5_q), .clk(Clock), .clr(Clear));
  Register #(.width(16)) r7_6 (.D(Write_Data), .en(and_7_out), .Q(r7_6_q), .clk(Clock), .clr(Clear));
  Register #(.width(16)) r8_7 (.D(Write_Data), .en(and_8_out), .Q(r8_7_q), .clk(Clock), .clr(Clear));
  Register #(.width(16)) t1_8 (.D(Write_Data), .en(and_9_out), .Q(t1_8_q), .clk(Clock), .clr(Clear));
  Register #(.width(16)) t2_9 (.D(Write_Data), .en(and_10_out), .Q(t2_9_q), .clk(Clock), .clr(Clear));
  Register #(.width(16)) t3_10 (.D(Write_Data), .en(and_11_out), .Q(t3_10_q), .clk(Clock), .clr(Clear));
  Register #(.width(16)) t4_11 (.D(Write_Data), .en(and_12_out), .Q(t4_11_q), .clk(Clock), .clr(Clear));
  Register #(.width(16)) t5_12 (.D(Write_Data), .en(and_13_out), .Q(t5_12_q), .clk(Clock), .clr(Clear));
  Register #(.width(16)) t6_13 (.D(Write_Data), .en(and_14_out), .Q(t6_13_q), .clk(Clock), .clr(Clear));
  Register #(.width(16)) t7_14 (.D(Write_Data), .en(and_15_out), .Q(t7_14_q), .clk(Clock), .clr(Clear));
  Register #(.width(16)) t8_15 (.D(Write_Data), .en(and_16_out), .Q(t8_15_q), .clk(Clock), .clr(Clear));
  Multiplexer #(.select(4), .width(16), .enable("false")) multiplexer_1 (
    .in0(r1_0_q), .in1(r2_1_q), .in2(r3_2_q), .in3(r4_3_q), .in4(r5_4_q), .in5(r6_5_q), .in6(r7_6_q),
    .in7(r8_7_q), .in8(t1_8_q), .in9(t2_9_q), .in10(t3_10_q), .in11(t4_11_q), .in12(t5_12_q), .in13(t6_13_q),
    .in14(t7_14_q), .in15(t8_15_q), .out(Read_Data_1), .sel(Read_Register_1));
  Multiplexer #(.select(4), .width(16), .enable("false")) multiplexer_2 (
    .in0(r1_0_q), .in1(r2_1_q), .in2(r3_2_q), .in3(r4_3_q), .in4(r5_4_q), .in5(r6_5_q), .in6(r7_6_q),
    .in7(r8_7_q), .in8(t1_8_q), .in9(t2_9_q), .in10(t3_10_q), .in11(t4_11_q), .in12(t5_12_q), .in13(t6_13_q),
    .in14(t7_14_q), .in15(t8_15_q), .out(Read_Data_2), .sel(Read_Register_2));
endmodule

module ALU_Final (
  input  Cin,
  input  [15:0] A,
  input  [15:0] B,
  input  Bin,
  input  [2:0] ALUop,
  output Cout,
  output [15:0] S,
  output Zero
);

  wire comparator_1_lt;
  wire [3:0] bit_extender_1_out;
  wire [15:0] adder_1_out, and_1_out, bit_extender_2_out, multiplexer_1_out, not_1_out, shifter_1_out;

  assign not_1_out = ~B;  // NOT_Gate not_1, 16 bits wide
  Multiplexer #(.width(16), .enable("false")) multiplexer_1 (
    .in0(B), .in1(not_1_out), .out(multiplexer_1_out), .sel(Bin));
  assign and_1_out = A & B;  // AND_Gate and_1, 16 bits wide
  Comparator #(.width(16)) comparator_1 (.a(A), .b(B), .lt(comparator_1_lt));  // open: gt, eq
  Bit_Extender #(.in_width(16), .out_width(4)) bit_extender_1 (.in(B), .out(bit_extender_1_out));
  assign bit_extender_2_out = {{15{1'b0}}, comparator_1_lt};  // Bit_Extender bit_extender_2
  Adder #(.width(16)) adder_1 (.a(A), .b(multiplexer_1_out), .out(adder_1_out), .cin(Cin), .cout(Cout));
  Shifter #(.width(16)) shifter_1 (.in(A), .\dist (bit_extender_1_out), .out(shifter_1_out));
  Multiplexer #(.select(3), .width(16), .enable("false")) multiplexer_2 (
    .in0(adder_1_out), .in1(and_1_out), .in2(bit_extender_2_out), .in3(adder_1_out), .in4(shifter_1_out),
    .out(S), .sel(ALUop));  // open: in5, in6, in7
  nor nor_1 (Zero, S[0], S[1], S[2], S[3], S[4], S[5], S[6], S[7], S[8], S[9], S[10], S[11], S[12], S[13], S[14], S[15]);
endmodule

module Datapath (
  input  in_1,
  input  in_2,
  output [15:0] out_3,
  output [3:0] RS,
  output [3:0] RT,
  output [15:0] out_6,
  output [15:0] out_7,
  output [3:0] RD
);

  wire alu_final_1_zero, and_1_out, control_unit_1_binv, control_unit_1_branch, control_unit_1_cin,
       control_unit_1_jump, control_unit_1_memread, control_unit_1_memtoreg, control_unit_1_memwrite,
       control_unit_1_ramen, control_unit_1_regdest, control_unit_1_rt_im, control_unit_1_writeen;
  wire [2:0] control_unit_1_aluop;
  wire [3:0] multiplexer_1_out;
  wire [15:0] alu_final_1_s, bit_extender_1_out, bit_extender_2_out, multiplexer_3_out, multiplexer_4_out,
       multiplexer_5_out, ram_1_data, register_1_q, register_file_1_read_data_2;
  wire [15:12] rom_1_data;

  Register #(.width(16)) register_1 (.D(multiplexer_4_out), .Q(register_1_q), .clk(in_2));  // open: en, clr
  Adder #(.width(16)) adder_1 (.a(16'h1), .b(register_1_q), .out(out_3));  // open: cin, cout
  ROM #(.addrWidth(16), .dataWidth(16)) rom_1 (.addr(register_1_q), .data({rom_1_data, RS, RT, RD}));  // open: sel
  Multiplexer #(.width(4), .enable("false")) multiplexer_1 (
    .in0(RD), .in1(RT), .out(multiplexer_1_out), .sel(control_unit_1_regdest));
  assign bit_extender_1_out = {{4{1'b0}}, {RS, RT, RD}};  // Bit_Extender bit_extender_1
  Register_File register_file_1 (
    .Write_Data(multiplexer_5_out), .Read_Register_1(RS), .Write_Register(multiplexer_1_out),
    .Read_Register_2(RT), .Write_Enable(control_unit_1_writeen), .Read_Data_1(out_6),
    .Read_Data_2(register_file_1_read_data_2), .Clock(in_2), .Clear(in_1));
  assign bit_extender_2_out = {{12{1'b0}}, RD};  // Bit_Extender bit_extender_2
  Multiplexer #(.width(16), .enable("false")) multiplexer_2 (
    .in0(register_file_1_read_data_2), .in1(bit_extender_2_out), .out(out_7), .sel(control_unit_1_rt_im));
  Control_Unit control_unit_1 (
    .in_1(rom_1_data), .ALUop(control_unit_1_aluop), .Cin(control_unit_1_cin), .Binv(control_unit_1_binv),
    .WriteEN(control_unit_1_writeen), .RamEN(control_unit_1_ramen), .MemWrite(control_unit_1_memwrite),
    .MemRead(control_unit_1_memread), .MemToReg(control_unit_1_memtoreg), .RT_IM(control_unit_1_rt_im),
    .RegDest(control_unit_1_regdest), .Branch(control_unit_1_branch), .Jump(control_unit_1_jump));
  ALU_Final alu_final_1 (
    .Cin(control_unit_1_cin), .Bin(control_unit_1_binv), .ALUop(control_unit_1_aluop), .S(alu_final_1_s),
    .Zero(alu_final_1_zero), .A(out_6), .B(out_7));  // open: Cout
  and and_1 (and_1_out, alu_final_1_zero, control_unit_1_branch);
  Multiplexer #(.width(16), .enable("false")) multiplexer_3 (
    .in0(out_3), .in1(bit_extender_2_out), .out(multiplexer_3_out), .sel(and_1_out));
  Multiplexer #(.width(16), .enable("false")) multiplexer_4 (
    .in0(multiplexer_3_out), .in1(bit_extender_1_out), .out(multiplexer_4_out), .sel(control_unit_1_jump));
  RAM #(.addrWidth(16), .dataWidth(16), .bus("separate")) ram_1 (
    .addr(alu_final_1_s), .din(register_file_1_read_data_2), .data(ram_1_data),
    .str(control_unit_1_memwrite), .sel(control_unit_1_ramen), .clk(in_2), .ld(control_unit_1_memread),
    .clr(in_1));
  Multiplexer #(.width(16), .enable("false")) multiplexer_5 (
    .in0(alu_final_1_s), .in1(ram_1_data), .out(multiplexer_5_out), .sel(control_unit_1_memtoreg));

  // Notes on the sheet:
  //   contents of rom_1 (hex, n*v repeats v):
  //   4400 4411 1551 3012 5257 9010 8008 6010
endmodule

module Control_Unit (
  input  [3:0] in_1,
  output [2:0] ALUop,
  output Cin,
  output Binv,
  output WriteEN,
  output RamEN,
  output MemWrite,
  output MemRead,
  output MemToReg,
  output RT_IM,
  output RegDest,
  output Jump,
  output Branch
);

  wire decoder_1_out0, decoder_1_out1, decoder_1_out2, decoder_1_out3, decoder_1_out6, decoder_1_out9,
       decoder_1_out11, decoder_1_out12, decoder_1_out13, decoder_1_out14, decoder_1_out15;

  Decoder #(.select(4), .enable("false")) decoder_1 (
    .out0(decoder_1_out0), .out1(decoder_1_out1), .out2(decoder_1_out2), .out3(decoder_1_out3),
    .out4(MemRead), .out5(Branch), .out6(decoder_1_out6), .out7(ALUop[2]), .out8(Jump),
    .out9(decoder_1_out9), .out10(MemWrite), .out11(decoder_1_out11), .out12(decoder_1_out12),
    .out13(decoder_1_out13), .out14(decoder_1_out14), .out15(decoder_1_out15), .sel(in_1));
  or or_1 (ALUop[0], decoder_1_out2, Branch);
  or or_2 (ALUop[1], decoder_1_out3, Branch);
  or or_3 (Cin, Branch, decoder_1_out9);
  or or_4 (Binv, decoder_1_out9, Branch);
  or or_5 (RamEN, MemRead, MemWrite);
  or or_6 (RT_IM, decoder_1_out1, MemRead, ALUop[2], MemWrite);
  or or_7 (RegDest, decoder_1_out1, MemRead, ALUop[2]);
  or or_8 (WriteEN, decoder_1_out1, decoder_1_out2, MemRead, decoder_1_out6, ALUop[2], decoder_1_out9);

  assign MemToReg = MemRead;
endmodule
